// Logisim project DLatch.circ as structural Verilog: 1 circuit, main circuit main
module main (
  input  Enable,
  input  Set,
  output Q,
  output nQ
);

  wire and_1_out, and_2_out, not_1_out;

  not not_1 (not_1_out, Set);
  and and_1 (and_1_out, not_1_out, Enable);
  and and_2 (and_2_out, Enable, Set);
  nor nor_1 (Q, and_1_out, nQ);
  nor nor_2 (nQ, Q, and_2_out);
endmodule
