// Logisim project everythingBagel.circ as structural Verilog: 4 circuits, main circuit main
module main (
  input  in_1,
  input  [7:0] a,
  input  [7:0] b,
  output [7:0] sum,
  output out_5
);

  _8_bitFullAdder u_8_bitfulladder_1 (.a(a), .b(b), .cIn(in_1), .cOut(out_5), .sum(sum));
endmodule

module halfAdder (
  input  a,
  input  b,
  output Sum,
  output cOut
);

  and and_1 (cOut, a, b);
  xor xor_1 (Sum, b, a);
endmodule

module _1_bitFullAdder (
  input  cIn,
  input  a,
  input  b,
  output sum,
  output cOut
);

  wire and_1_out, and_2_out, xor_1_out;

  xor xor_1 (xor_1_out, a, b);
  and and_1 (and_1_out, a, b);
  and and_2 (and_2_out, cIn, xor_1_out);
  xor xor_2 (sum, cIn, xor_1_out);
  or or_1 (cOut, and_2_out, and_1_out);
endmodule

module _8_bitFullAdder (
  input  cIn,
  input  [7:0] a,
  input  [7:0] b,
  output [7:0] sum,
  output cOut
);

  wire n1_bitfulladder_1_cout, n1_bitfulladder_2_cout, n1_bitfulladder_3_cout, n1_bitfulladder_4_cout,
       n1_bitfulladder_5_cout, n1_bitfulladder_6_cout, n1_bitfulladder_7_cout;

  _1_bitFullAdder u_1_bitfulladder_1 (.a(a[0]), .b(b[0]), .sum(sum[0]), .cIn(cIn), .cOut(n1_bitfulladder_1_cout));
  _1_bitFullAdder u_1_bitfulladder_2 (
    .a(a[1]), .b(b[1]), .sum(sum[1]), .cIn(n1_bitfulladder_1_cout), .cOut(n1_bitfulladder_2_cout));
  _1_bitFullAdder u_1_bitfulladder_3 (
    .a(a[2]), .b(b[2]), .sum(sum[2]), .cIn(n1_bitfulladder_2_cout), .cOut(n1_bitfulladder_3_cout));
  _1_bitFullAdder u_1_bitfulladder_4 (
    .a(a[3]), .b(b[3]), .sum(sum[3]), .cIn(n1_bitfulladder_3_cout), .cOut(n1_bitfulladder_4_cout));
  _1_bitFullAdder u_1_bitfulladder_5 (
    .a(a[4]), .b(b[4]), .sum(sum[4]), .cIn(n1_bitfulladder_4_cout), .cOut(n1_bitfulladder_5_cout));
  _1_bitFullAdder u_1_bitfulladder_6 (
    .a(a[5]), .b(b[5]), .sum(sum[5]), .cIn(n1_bitfulladder_5_cout), .cOut(n1_bitfulladder_6_cout));
  _1_bitFullAdder u_1_bitfulladder_7 (
    .a(a[6]), .b(b[6]), .sum(sum[6]), .cIn(n1_bitfulladder_6_cout), .cOut(n1_bitfulladder_7_cout));
  _1_bitFullAdder u_1_bitfulladder_8 (.a(a[7]), .b(b[7]), .sum(sum[7]), .cIn(n1_bitfulladder_7_cout), .cOut(cOut));
endmodule
