// Logisim project fullAdder4bit.circ as structural Verilog: 1 circuit, main circuit main
module main (
  input  cIn,
  input  a,
  input  b,
  input  a_2,
  input  b_2,
  input  a_3,
  input  b_3,
  input  a_4,
  input  b_4,
  output sum,
  output sum_2,
  output sum_3,
  output sum_4,
  output cOut
);

  wire and_1_out, and_2_out, and_3_out, and_4_out, and_5_out, and_6_out, and_7_out, and_8_out, or_1_out,
       or_2_out, or_3_out, xor_1_out, xor_2_out, xor_3_out, xor_4_out;

  xor xor_1 (xor_1_out, a, b);
  and and_1 (and_1_out, a, b);
  xor xor_2 (xor_2_out, a_2, b_2);
  and and_2 (and_2_out, a_2, b_2);
  xor xor_3 (xor_3_out, a_3, b_3);
  and and_3 (and_3_out, a_3, b_3);
  xor xor_4 (xor_4_out, a_4, b_4);
  and and_4 (and_4_out, a_4, b_4);
  and and_5 (and_5_out, cIn, xor_1_out);
  and and_6 (and_6_out, or_1_out, xor_2_out);
  and and_7 (and_7_out, or_2_out, xor_3_out);
  and and_8 (and_8_out, or_3_out, xor_4_out);
  xor xor_5 (sum, cIn, xor_1_out);
  or or_1 (or_1_out, and_5_out, and_1_out);
  xor xor_6 (sum_2, or_1_out, xor_2_out);
  or or_2 (or_2_out, and_6_out, and_2_out);
  xor xor_7 (sum_3, or_2_out, xor_3_out);
  or or_3 (or_3_out, and_7_out, and_3_out);
  xor xor_8 (sum_4, or_3_out, xor_4_out);
  or or_4 (cOut, and_8_out, and_4_out);
endmodule
