// Logisim project fullAdder.circ as structural Verilog: 1 circuit, main circuit main
module main (
  input  cIn,
  input  a,
  input  b,
  output sum,
  output cOut
);

  wire and_1_out, and_2_out, xor_1_out;

  xor xor_1 (xor_1_out, a, b);
  and and_1 (and_1_out, a, b);
  and and_2 (and_2_out, cIn, xor_1_out);
  xor xor_2 (sum, cIn, xor_1_out);
  or or_1 (cOut, and_2_out, and_1_out);
endmodule
