// Logisim project halfAdder.circ as structural Verilog: 1 circuit, main circuit main
module main (
  input  a,
  input  b,
  output sum,
  output cOut
);

  xor xor_1 (sum, a, b);
  and and_1 (cOut, a, b);
endmodule
