// Logisim project rippleCounter.circ as structural Verilog: 1 circuit, main circuit main
module main (
  input  in_1,
  output out_2,
  output out_3,
  output out_4,
  output out_5
);

  wire clock_1_out, not_1_out, not_2_out, not_3_out, not_4_out;

  Clock clock_1 (.out(clock_1_out));
  not not_1 (not_1_out, clock_1_out);
  T_Flip_Flop #(.trigger("falling")) t_ff_1 (.clk(not_1_out), .T(in_1), .Q(out_2));  // open: Qn, preset, reset, en
  T_Flip_Flop t_ff_2 (.clk(not_2_out), .T(in_1), .Q(out_3));  // open: Qn, preset, reset, en
  not not_2 (not_2_out, out_2);
  not not_3 (not_3_out, out_3);
  T_Flip_Flop t_ff_3 (.clk(not_3_out), .T(in_1), .Q(out_4));  // open: Qn, preset, reset, en
  not not_4 (not_4_out, out_4);
  T_Flip_Flop t_ff_4 (.clk(not_4_out), .T(in_1), .Q(out_5));  // open: Qn, preset, reset, en
endmodule
